// Digital circuit cpu.dig as structural Verilog
module cpu (
  input  clk,
  input  fetch_en,
  input  jmp_en
);

  wire decode_1_p3, decode_1_p4, decode_1_p5, decode_1_p6, decode_1_p7, decode_1_p8, decode_1_p9,
       Decode_Execute_p8, Decode_Execute_p9, Decode_Execute_p10, Execute_Memory_p7, Execute_Memory_p8,
       RegFile_p8, RegFile_p9;
  wire [1:0] Execute_Memory_p9, Memory_Writeback_p5;
  wire [3:0] Decode_Execute_p11;
  wire [15:0] alu_1_q, Decode_Execute_p12, Decode_Execute_p13, Execute_Memory_p10, Execute_Memory_p11,
       Fetch_Decode_inst_2, mem_1_q, Memory_Writeback_p6, Memory_Writeback_p7, RegFile_p5, RegFile_p7;

  f_de Fetch_Decode (.Inst(mem_1_q), .clk(clk), .Inst_2(Fetch_Decode_inst_2));
  // decode decode_1: pin names not known; wires that end beside it: Fetch_Decode_inst_2, clk, decode_1_p3, decode_1_p4, decode_1_p5, decode_1_p6, decode_1_p7, decode_1_p8, decode_1_p9
  // operands RegFile: pin names not known; wires that end beside it: decode_1_p7, decode_1_p8, decode_1_p9, Memory_Writeback_p5[1], RegFile_p5, clk, RegFile_p7, RegFile_p8, RegFile_p9
  // de_ex Decode_Execute: pin names not known; wires that end beside it: decode_1_p3, decode_1_p4, decode_1_p5, decode_1_p6, RegFile_p8, RegFile_p9, clk, Decode_Execute_p8, Decode_Execute_p9, Decode_Execute_p10, Decode_Execute_p11, Decode_Execute_p12, Decode_Execute_p13
  alu alu_1 (.AluOp(Decode_Execute_p11), .Rhs(Decode_Execute_p12), .clk(clk), .Lhs(Decode_Execute_p13), .Q(alu_1_q));
  // ex_mem Execute_Memory: pin names not known; wires that end beside it: Decode_Execute_p8, Decode_Execute_p9, Decode_Execute_p10, Decode_Execute_p13, clk, alu_1_q, Execute_Memory_p7, Execute_Memory_p8, Execute_Memory_p9, Execute_Memory_p10, Execute_Memory_p11
  pc pc_1 (.clk(clk), .fetch(fetch_en), .addr(alu_1_q), .jmp_en(jmp_en), .Q(RegFile_p5));
  mem mem_1 (
    .MemRdEn(Execute_Memory_p8), .MemWrEn(Execute_Memory_p9), .DataIn(Execute_Memory_p10),
    .Addr(Execute_Memory_p11), .clk(clk), .Q(mem_1_q));
  // mem_wb Memory_Writeback: pin names not known; wires that end beside it: Execute_Memory_p7, clk, Execute_Memory_p11, mem_1_q, Memory_Writeback_p5, Memory_Writeback_p6, Memory_Writeback_p7
  Multiplexer #(.Bits(16)) multiplexer_1 (
    .sel(Memory_Writeback_p5[0]), .in_0(Memory_Writeback_p6), .in_1(Memory_Writeback_p7), .out(RegFile_p7));
endmodule
