// Digital circuit de_ex.dig as structural Verilog
module de_ex (
  input  [3:0] AluOp,
  input  [15:0] Lhs,
  input  [15:0] Rhs,
  input  clk,
  output [15:0] Lhs_2,
  output [15:0] Rhs_2,
  output [3:0] AluOp_2
);

  Register #(.Bits(4)) register_1 (.D(AluOp), .C(clk), .en(1'b1), .Q(AluOp_2));
  Register #(.Bits(16)) register_2 (.D(Lhs), .C(clk), .en(1'b1), .Q(Lhs_2));
  Register #(.Bits(16)) register_3 (.D(Rhs), .C(clk), .en(1'b1), .Q(Rhs_2));
endmodule
