// Digital circuit decode.dig as structural Verilog
module decode (
  input  [15:0] Inst,
  input  clk,
  output [2:0] MemMode,
  output [1:0] WbMode,
  output [3:0] RegA,
  output [3:0] RegB,
  output [15:0] Imm,
  output [2:0] JmpCond,
  output [3:0] AluOp
);

  wire [15:0] Decoder_d;

  ROM #(.AddrBits(16), .Bits(16)) Decoder (
    .A(Inst), .sel(1'b1), .D({Decoder_d[15:7], WbMode, MemMode, Decoder_d[1:0]}));
  Multiplexer #(.Bits(4)) multiplexer_1 (.sel(Decoder_d[1]), .in_0(Inst[11:8]), .in_1(4'b0000), .out(AluOp));
  Multiplexer #(.Bits(3)) multiplexer_2 (.sel(Decoder_d[0]), .in_0({Inst[9], Inst[7:6]}), .in_1(3'b000), .out(JmpCond));

  assign Imm = 16'h1;
  assign RegA = Inst[7:4];
  assign RegB = Inst[3:0];

  // Other names for the same wires on the sheet: b0 = Inst[0]; b1 = Inst[1]; b2 = Inst[2]; b3 = Inst[3]; b4 = Inst[4];
  //   b5 = Inst[5]; b6 = Inst[6]; b7 = Inst[7]; b8 = Inst[8]; b9 = Inst[9]; b10 = Inst[10]; b11 = Inst[11];
  //   b12 = Inst[12]; b13 = Inst[13]; b14 = Inst[14]; b15 = Inst[15]
endmodule
