// Digital circuit fetch.dig as structural Verilog
module fetch (
  input  clk,
  output [7:0] Inst
);

  wire [7:0] add_1_s, PC_q;

  Register #(.Bits(8)) PC (.D(add_1_s), .C(clk), .en(1'b1), .Q(PC_q));
  Add #(.Bits(8)) add_1 (.a(8'h1), .b(PC_q), .c_i(1'b0), .s(add_1_s));  // open: c_o
  // Probe on PC_q
  ROM #(.AddrBits(8), .Bits(8), .isProgramMemory("true")) rom_1 (.A(PC_q), .sel(1'b1), .D(Inst));

  // Notes on the sheet:
  //   clk: Hz: 5
  //   contents of rom_1 (hex, n*v repeats v):
  //   10,d,c,b,a,9,8,7,6,5,4,3,2,1
endmodule
